# Fritzing sketch 2buttons_2leds (saved by Fritzing 0.9.1b)
breadboards: 1

parts:
  S1 = Momentary Switch [package=ksa_sealed_tac_switch]
  S2 = Momentary Switch [package=ksa_sealed_tac_switch]
  LED1 = LED - 5mm [color="Red (633nm)" package="5 mm [THT]"]
  LED2 = LED - 5mm [color="Green (555nm)" package="5 mm [THT]"]
  R1 = Resistor [tolerance=±5% resistance=220 package="0805 [SMD]"]
  R2 = Resistor [tolerance=±5% resistance=220 package="0805 [SMD]"]
  Part1 = Arduino Uno (Rev3) - ICSP
  R3 = Resistor [tolerance=±5% resistance=220 package="0805 [SMD]"]
  R4 = Resistor [tolerance=±5% resistance=220 package="0805 [SMD]"]

nets:
  N1: S1.2, S2.2, Part1.5V
  N2: S1.4, Part1.D2, R3.Pin_1
  N3: S2.4, Part1.D3_PWM, R4.Pin_1
  N4: LED1.cathode, LED2.cathode, Part1.GND, R3.Pin_0, R4.Pin_0
  N5: LED1.anode, R1.Pin_1
  N6: LED2.anode, R2.Pin_1
  N7: R1.Pin_0, Part1.D4
  N8: R2.Pin_0, Part1.D5_PWM
